# Fritzing sketch eletricSchema (saved by Fritzing 0.9.3b)
breadboards: 1

parts:
  S1 = H-Bridge with L298N
  Part1 = Arduino Uno (Rev3)
  T1 = LM35 Temperature Sensor [package="TO92 [THT]"]
  U1 = RELAY [package=relay-g5q]  # not connected
  M2 = Stepper Motor - Bipolar

nets:
  GND: S1.GND, Part1.GND, T1.GND
  N1: S1.ENA, S1.ENB, Part1.5V, T1.+Vs
  N2: S1.IN1, Part1.D2
  N3: S1.IN2, Part1.D3_PWM
  N4: S1.IN3, Part1.D4
  N5: S1.IN4, Part1.D5_PWM
  N6: S1.M1-01, M2.C
  N7: S1.M1-02, M2.A
  N8: S1.M2-01, M2.D
  N9: S1.M2-02, M2.B
  N10: Part1.A0, T1.Vout

custom parts:
  H-Bridge with L298N: h-bridge
